# Fritzing sketch RGWR (saved by Fritzing 0.9.3b)
breadboards: 1

parts:
  부품1 = Thumb Joystick
  Grove1 = Grove OLED 128x96
  S1 = Pushbutton [package="[SMD]"]
  S2 = Pushbutton [package="[THT]"]
  부품2 = Arduino Leonardo (Rev3b)

nets:
  GND: 부품1.GND, Grove1.GND, S1.Pin_1, S1.Pin_2, S2.Pin_3, S2.Pin_4, 부품2.GND
  N1: 부품1.HORZ, 부품2.A1
  N2: 부품1.VERT, 부품2.A0
  VCC: 부품1.VCC, Grove1.VCC, 부품2.5V
  N3: Grove1.SDA, 부품2.D2/SDA
  N4: Grove1.SCL, 부품2.D3_PWM/SCL
  N5: S1.Pin_3, S1.Pin_4, 부품2.D7
  N6: S2.Pin_1, S2.Pin_2, 부품2.D6_PWM/A7
